# Fritzing sketch 01 (saved by Fritzing 0.9.3b)
breadboards: 1

parts:
  Súčiastka1 = Arduino Uno (Rev3)
  R1 = Resistor [tolerance=±5% resistance=220 package=THT]
  LED1 = smd LED [color="Red (635nm)" package="0603 [SMD]"]

nets:
  N1: Súčiastka1.D9_PWM, R1.Pin_0
  N2: Súčiastka1.3V3, LED1.cathode
  N3: R1.Pin_1, LED1.anode
