# Fritzing sketch 04 (saved by Fritzing 0.9.3b)
breadboards: 1

parts:
  Súčiastka1 = Arduino Uno (Rev3)
  RHT1 = Humidity and Temperature Sensor RHT03

nets:
  N1: Súčiastka1.D10_PWM/SS, RHT1.Data-signal
  5V: Súčiastka1.5V, RHT1.Vcc
  N2: Súčiastka1.GND, RHT1.GND_2
