# Fritzing sketch 05 (saved by Fritzing 0.9.3b)
breadboards: 1

parts:
  Súčiastka1 = Arduino Uno (Rev3)
  Súčiastka2 = Real Time Clock Module - DS1307 RTC Breakout Board

nets:
  N1: Súčiastka1.A4/SDA, Súčiastka2.SDA
  N2: Súčiastka1.A5/SCL, Súčiastka2.SCL
  5V: Súčiastka1.5V, Súčiastka2.5V
  GND: Súčiastka1.GND, Súčiastka2.GND
